// Logisim project tmi.circ as structural Verilog: 4 circuits, main circuit cell
module main (
);

  wire cell_1_clk_2, cell_1_is_active_2, cell_1_set_head, cell_2_clk_2, cell_2_is_active, cell_2_is_active_2,
       cell_2_set_head, cell_2_set_tail, cell_3_clk_2, cell_3_is_active, cell_3_is_active_2, cell_3_set_head,
       cell_3_set_tail, cell_4_clk_2, cell_4_is_active, cell_4_is_active_2, cell_4_set_head, cell_4_set_tail,
       cell_5_is_active, cell_5_set_tail, clock_1_out, cpu_1_cell_clk, cpu_1_fake_act, cpu_1_is_inited,
       cpu_1_is_on, cpu_1_kbd_clk, cpu_1_tape_next, cpu_1_tape_prev, cpu_1_tty_clk, cpu_1_wait_kbd,
       keyboard_1_avail, START_out;
  wire [2:0] cell_1_cmd_2, cell_1_dbg_led, cell_2_cmd_2, cell_2_dbg_led, cell_3_cmd_2, cell_3_dbg_led,
       cell_4_cmd_2, cell_4_dbg_led, cell_5_cmd_2, cell_5_dbg_led, cpu_1_cmd;
  wire [3:0] cell_1_dbg_mem, cell_1_dbg_mem_2, cell_2_dbg_mem, cell_2_dbg_mem_2, cell_3_dbg_mem,
       cell_3_dbg_mem_2, cell_4_dbg_mem, cell_4_dbg_mem_2, rom_1_data, tape_1_bf_cmd;
  wire [6:0] cpu_1_disp, keyboard_1_data;
  wire [7:0] cell_1_data_in_2, cell_1_data_out_2, cell_2_data_in_2, cell_2_data_out_2, cell_3_data_in_2,
       cell_3_data_out_2, cell_4_data_in_2, cell_4_data_out_2, cell_5_data_in_2, cell_5_data_out_2,
       cell_5_dbg_mem, cpu_1_data_to_cell;
  wire [11:0] tape_1_address;

  LED NEED_INPUT (.in(cpu_1_wait_kbd));
  tape tape_1 (
    .ADDRESS(tape_1_address), .DATA(rom_1_data), .BF_CMD(tape_1_bf_cmd), .BF_NEXT(cpu_1_tape_next),
    .BF_PREV(cpu_1_tape_prev));
  Clock clock_1 (.out(clock_1_out));
  Button START (.out(START_out));
  Keyboard keyboard_1 (.clk(cpu_1_kbd_clk), .avail(keyboard_1_avail), .data(keyboard_1_data));  // open: re, clr
  ROM #(.addrWidth(12), .dataWidth(4)) rom_1 (.addr(tape_1_address), .data(rom_1_data));  // open: sel
  ROM #(.addrWidth(12), .dataWidth(4)) rom_2 ();  // open: addr, data, sel
  LED IS_ON (.in(cpu_1_is_on));
  LED IS_INITED (.in(cpu_1_is_inited));
  cpu cpu_1 (
    .CUR_BF(tape_1_bf_cmd), .TAPE_NEXT(cpu_1_tape_next), .TAPE_PREV(cpu_1_tape_prev),
    .IS_INITED(cpu_1_is_inited), .IS_ON(cpu_1_is_on), .DISP(cpu_1_disp), .TTY_CLK(cpu_1_tty_clk),
    .CLK(clock_1_out), .TURN_ON(START_out), .WAIT_KBD(cpu_1_wait_kbd), .KBD_CLK(cpu_1_kbd_clk),
    .CHAR(keyboard_1_data), .HAS_CHAR(keyboard_1_avail), .FAKE_ACT(cpu_1_fake_act),
    .DATA_TO_CELL(cpu_1_data_to_cell), .DATA_FROM_CELL(cell_1_data_out_2), .CMD(cpu_1_cmd),
    .CELL_CLK(cpu_1_cell_clk));
  LED HAS_INPUT (.in(keyboard_1_avail));
  TTY tty_1 (.data(cpu_1_disp), .clk(cpu_1_tty_clk));  // open: we, clr
  DotMatrix #(.matrixcols(3), .matrixrows(1)) dotmatrix_1 (
    .col0(cell_1_dbg_led[0]), .col1(cell_1_dbg_led[1]), .col2(cell_1_dbg_led[2]));
  Hex_Digit_Display hex_digit_display_1 (.value(cell_1_dbg_mem_2));  // open: dp
  Hex_Digit_Display hex_digit_display_2 (.value(keyboard_1_data[3:0]));  // open: dp
  Hex_Digit_Display hex_digit_display_3 (.value({1'b0, keyboard_1_data[6:4]}));  // open: dp
  \cell  cell_1 (
    .IS_ACTIVE_LEFT(cpu_1_fake_act), .DATA_IN(cpu_1_data_to_cell), .DATA_OUT_2(cell_1_data_out_2),
    .CMD(cpu_1_cmd), .CLK(cpu_1_cell_clk), .IS_TAIL(cell_2_set_tail), .SET_HEAD(cell_1_set_head),
    .IS_ACTIVE_RIGHT(cell_2_is_active), .IS_ACTIVE_2(cell_1_is_active_2), .DATA_IN_2(cell_1_data_in_2),
    .DATA_OUT(cell_2_data_out_2), .CMD_2(cell_1_cmd_2), .CLK_2(cell_1_clk_2),
    .DBG_MEM({cell_1_dbg_mem_2, cell_1_dbg_mem}), .DBG_LED(cell_1_dbg_led));  // open: SET_TAIL, IS_HEAD, IS_ACTIVE
  Hex_Digit_Display hex_digit_display_4 (.value(cell_1_dbg_mem));  // open: dp
  \cell  cell_2 (
    .SET_TAIL(cell_2_set_tail), .IS_HEAD(cell_1_set_head), .IS_ACTIVE(cell_2_is_active),
    .IS_ACTIVE_LEFT(cell_1_is_active_2), .DATA_IN(cell_1_data_in_2), .DATA_OUT_2(cell_2_data_out_2),
    .CMD(cell_1_cmd_2), .CLK(cell_1_clk_2), .IS_TAIL(cell_3_set_tail), .SET_HEAD(cell_2_set_head),
    .IS_ACTIVE_RIGHT(cell_3_is_active), .IS_ACTIVE_2(cell_2_is_active_2), .DATA_IN_2(cell_2_data_in_2),
    .DATA_OUT(cell_3_data_out_2), .CMD_2(cell_2_cmd_2), .CLK_2(cell_2_clk_2),
    .DBG_MEM({cell_2_dbg_mem_2, cell_2_dbg_mem}), .DBG_LED(cell_2_dbg_led));
  DotMatrix #(.matrixcols(3), .matrixrows(1)) dotmatrix_2 (
    .col0(cell_2_dbg_led[0]), .col1(cell_2_dbg_led[1]), .col2(cell_2_dbg_led[2]));
  Hex_Digit_Display hex_digit_display_5 (.value(cell_2_dbg_mem));  // open: dp
  Hex_Digit_Display hex_digit_display_6 (.value(cell_2_dbg_mem_2));  // open: dp
  DotMatrix #(.matrixcols(3), .matrixrows(1)) dotmatrix_3 (
    .col0(cell_3_dbg_led[0]), .col1(cell_3_dbg_led[1]), .col2(cell_3_dbg_led[2]));
  Hex_Digit_Display hex_digit_display_7 (.value(cell_3_dbg_mem_2));  // open: dp
  \cell  cell_3 (
    .SET_TAIL(cell_3_set_tail), .IS_HEAD(cell_2_set_head), .IS_ACTIVE(cell_3_is_active),
    .IS_ACTIVE_LEFT(cell_2_is_active_2), .DATA_IN(cell_2_data_in_2), .DATA_OUT_2(cell_3_data_out_2),
    .CMD(cell_2_cmd_2), .CLK(cell_2_clk_2), .IS_TAIL(cell_4_set_tail), .SET_HEAD(cell_3_set_head),
    .IS_ACTIVE_RIGHT(cell_4_is_active), .IS_ACTIVE_2(cell_3_is_active_2), .DATA_IN_2(cell_3_data_in_2),
    .DATA_OUT(cell_4_data_out_2), .CMD_2(cell_3_cmd_2), .CLK_2(cell_3_clk_2),
    .DBG_MEM({cell_3_dbg_mem_2, cell_3_dbg_mem}), .DBG_LED(cell_3_dbg_led));
  Hex_Digit_Display hex_digit_display_8 (.value(cell_3_dbg_mem));  // open: dp
  \cell  cell_4 (
    .SET_TAIL(cell_4_set_tail), .IS_HEAD(cell_3_set_head), .IS_ACTIVE(cell_4_is_active),
    .IS_ACTIVE_LEFT(cell_3_is_active_2), .DATA_IN(cell_3_data_in_2), .DATA_OUT_2(cell_4_data_out_2),
    .CMD(cell_3_cmd_2), .CLK(cell_3_clk_2), .IS_TAIL(cell_5_set_tail), .SET_HEAD(cell_4_set_head),
    .IS_ACTIVE_RIGHT(cell_5_is_active), .IS_ACTIVE_2(cell_4_is_active_2), .DATA_IN_2(cell_4_data_in_2),
    .DATA_OUT(cell_5_data_out_2), .CMD_2(cell_4_cmd_2), .CLK_2(cell_4_clk_2),
    .DBG_MEM({cell_4_dbg_mem_2, cell_4_dbg_mem}), .DBG_LED(cell_4_dbg_led));
  DotMatrix #(.matrixcols(3), .matrixrows(1)) dotmatrix_4 (
    .col0(cell_4_dbg_led[0]), .col1(cell_4_dbg_led[1]), .col2(cell_4_dbg_led[2]));
  Hex_Digit_Display hex_digit_display_9 (.value(cell_4_dbg_mem));  // open: dp
  Hex_Digit_Display hex_digit_display_10 (.value(cell_4_dbg_mem_2));  // open: dp
  DotMatrix #(.matrixcols(3), .matrixrows(1)) dotmatrix_5 (
    .col0(cell_5_dbg_led[0]), .col1(cell_5_dbg_led[1]), .col2(cell_5_dbg_led[2]));
  Hex_Digit_Display hex_digit_display_11 (.value(cell_5_dbg_mem[7:4]));  // open: dp
  \cell  cell_5 (
    .SET_TAIL(cell_5_set_tail), .IS_HEAD(cell_4_set_head), .IS_ACTIVE(cell_5_is_active),
    .IS_ACTIVE_LEFT(cell_4_is_active_2), .DATA_IN(cell_4_data_in_2), .DATA_OUT_2(cell_5_data_out_2),
    .CMD(cell_4_cmd_2), .CLK(cell_4_clk_2), .DATA_IN_2(cell_5_data_in_2), .CMD_2(cell_5_cmd_2),
    .DBG_MEM(cell_5_dbg_mem), .DBG_LED(cell_5_dbg_led));  // open: IS_TAIL, SET_HEAD, IS_ACTIVE_RIGHT, IS_ACTIVE_2, DATA_OUT, CLK_2
  Hex_Digit_Display hex_digit_display_12 (.value(cell_5_dbg_mem[3:0]));  // open: dp
  Hex_Digit_Display hex_digit_display_13 (.value(cell_5_data_in_2[7:4]));  // open: dp
  Hex_Digit_Display hex_digit_display_14 (.value({1'b0, cell_5_cmd_2}));  // open: dp
  Hex_Digit_Display hex_digit_display_15 (.value(cell_5_data_in_2[3:0]));  // open: dp

  // Notes on the sheet:
  //   [Hello, world]
  //   Hello, world
  //   contents of rom_1 (hex, n*v repeats v):
  //   10*6 1 3 7*6 3 10*6 3 6 6 6 3 6 4*2 7 0 3 6 6 4 3 6 4 7*6 4 4 6 6 6 4 3 6 6 4 2 2 15*6 4 3 4 6 6 6 4
  //   6*7 4 8*7 4 3 6 4 3 4 8
  //   contents of rom_2 (hex, n*v repeats v):
  //   72*6 4 29*6 4 7*6 4 4 6 6 6 4 79*7 4 55*6 4 24*6 4 6 6 6 4 6*7 4 8*7 4 67*7 4 23*7 4 8
endmodule

// memcell
module \cell  (
  input  IS_TAIL,
  input  IS_HEAD,
  input  IS_ACTIVE_RIGHT,
  input  IS_ACTIVE_LEFT,
  input  [7:0] DATA_IN,
  input  [7:0] DATA_OUT,
  input  [2:0] CMD,
  input  CLK,
  output SET_TAIL,
  output SET_HEAD,
  output IS_ACTIVE,
  output IS_ACTIVE_2,
  output [7:0] DATA_IN_2,
  output [7:0] DATA_OUT_2,
  output [2:0] CMD_2,
  output CLK_2,
  output [7:0] DBG_MEM,
  output [2:0] DBG_LED
);

  wire and_1_out, and_2_out, and_6_out, bitselector_1_out, bitselector_2_out, COUNT, decoder_1_out0, LOAD,
       minus_ACT, not_1_out, not_2_out, not_3_out, not_4_out, not_5_out, plus_1__1, plus_ACT, R_W, RST,
       s_r_ff_1_q, tunnel, WRITE;
  wire [7:0] controlled_buffer_5_out;

  Decoder #(.select(2), .disabled(0), .enable("false")) decoder_1 (
    .out0(decoder_1_out0), .out1(tunnel), .out2(R_W), .out3(plus_1__1), .sel(CMD[2:1]));
  and and_1 (and_1_out, CMD[0], decoder_1_out0);
  not not_1 (not_1_out, bitselector_1_out);
  BitSelector #(.width(2)) bitselector_1 (.in({IS_TAIL, IS_HEAD}), .out(bitselector_1_out), .sel(CMD[0]));
  not not_2 (not_2_out, DBG_LED[1]);
  BitSelector #(.width(2)) bitselector_2 (
    .in({IS_ACTIVE_LEFT, IS_ACTIVE_RIGHT}), .out(bitselector_2_out), .sel(CMD[0]));
  and and_2 (and_2_out, plus_1__1, DBG_LED[1]);
  and and_3 (WRITE, R_W, CMD[0], DBG_LED[1]);
  Pull_Resistor #(.pull(1)) pull_resistor_1 (.node(IS_HEAD));
  Pull_Resistor pull_resistor_2 (.node(IS_ACTIVE_LEFT));
  D_Flip_Flop d_ff_1 (.clk(CLK), .D(and_1_out), .Q(RST), .reset(not_3_out));  // open: Qn, preset, en
  not not_3 (not_3_out, and_1_out);
  assign LOAD = and_2_out ? CMD[0] : 1'bz;  // Controlled_Buffer controlled_buffer_1
  assign COUNT = and_2_out ? 1'b1 : 1'bz;  // Controlled_Buffer controlled_buffer_2
  assign LOAD = WRITE ? 1'b1 : 1'bz;  // Controlled_Buffer controlled_buffer_3
  assign COUNT = WRITE ? 1'b0 : 1'bz;  // Controlled_Buffer controlled_buffer_4
  Pull_Resistor pull_resistor_3 (.node(DATA_IN));
  Pull_Resistor pull_resistor_4 (.node(CMD));
  Pull_Resistor pull_resistor_5 (.node(CLK));
  and and_4 (minus_ACT, DBG_LED[1], tunnel, not_1_out);
  and and_5 (plus_ACT, not_2_out, tunnel, bitselector_2_out);
  assign controlled_buffer_5_out = WRITE ? DATA_IN : 8'bz;  // Controlled_Buffer controlled_buffer_5
  Pull_Resistor #(.pull(1)) pull_resistor_6 (.node(IS_TAIL));
  Pull_Resistor pull_resistor_7 (.node(IS_ACTIVE_RIGHT));
  S_R_Flip_Flop s_r_ff_1 (.S(plus_ACT), .clk(CLK), .R(minus_ACT), .Q(s_r_ff_1_q), .reset(RST));  // open: Qn, preset, en
  Pull_Resistor pull_resistor_8 (.node(LOAD));
  Counter counter_1 (
    .load(LOAD), .D(controlled_buffer_5_out), .count(COUNT), .Q(DBG_MEM), .clk(CLK), .clr(RST));  // open: carry
  Pull_Resistor pull_resistor_9 (.node(COUNT));
  not not_4 (not_4_out, CLK);
  D_Flip_Flop d_ff_2 (.clk(not_4_out), .D(s_r_ff_1_q), .Q(DBG_LED[1]), .reset(RST));  // open: Qn, preset, en
  assign DATA_OUT = and_6_out ? DBG_MEM : 8'bz;  // Controlled_Buffer controlled_buffer_6
  and and_6 (and_6_out, not_5_out, DBG_LED[1], R_W);
  not not_5 (not_5_out, CMD[0]);

  assign CLK_2 = CLK;
  assign CMD_2 = CMD;
  assign DATA_IN_2 = DATA_IN;
  assign DATA_OUT_2 = DATA_OUT;
  assign {DBG_LED[2], DBG_LED[0]} = {IS_TAIL, IS_HEAD};
  assign IS_ACTIVE = DBG_LED[1];
  assign IS_ACTIVE_2 = DBG_LED[1];
  assign SET_HEAD = 1'b0;
  assign SET_TAIL = 1'b0;

  // Other names for the same wires on the sheet: AR = IS_ACTIVE_RIGHT; AL = IS_ACTIVE_LEFT; HEAD = IS_HEAD;
  //   ACT = DBG_LED[1]; TAIL = IS_TAIL; IN[7:0] = DATA_IN; OUT[7:0] = DATA_OUT
endmodule

module tape (
  input  [3:0] DATA,
  input  BF_NEXT,
  input  BF_PREV,
  output [11:0] ADDRESS,
  output [3:0] BF_CMD
);

  wire or_1_out;

  or or_1 (or_1_out, BF_PREV, BF_NEXT);
  Pull_Resistor pull_resistor_1 (.node(BF_NEXT));
  Pull_Resistor pull_resistor_2 (.node(BF_PREV));
  Counter #(.width(12), .max('hfff)) counter_1 (
    .load(BF_PREV), .count(or_1_out), .Q(ADDRESS), .clk(or_1_out));  // open: D, carry, clr

  assign BF_CMD = DATA;

  // Other names for the same wires on the sheet: ADDR[11:0] = ADDRESS; NEXT = BF_NEXT; PREV = BF_PREV
endmodule

module cpu (
  input  [3:0] CUR_BF,
  input  [7:0] DATA_FROM_CELL,
  input  CLK,
  input  TURN_ON,
  input  [6:0] CHAR,
  input  HAS_CHAR,
  output IS_INITED,
  output IS_ON,
  output [6:0] DISP,
  output TTY_CLK,
  output FAKE_ACT,
  output [7:0] DATA_TO_CELL,
  output TAPE_NEXT,
  output TAPE_PREV,
  output [2:0] CMD,
  output CELL_CLK,
  output WAIT_KBD,
  output KBD_CLK
);

  wire and_1_out, and_2_out, and_3_out, and_4_out, and_5_out, and_6_out, and_7_out, and_8_out, and_9_out,
       and_10_out, and_11_out, and_12_out, and_13_out, and_14_out, and_15_out, and_17_out, and_18_out,
       and_19_out, and_20_out, CELL_ZERO, CLEAR_ACT, comparator_22_eq, IS_EXEC, IS_EXECR, IS_EXECW0,
       IS_EXECW1, IS_IN_CMD, IS_INIT0, IS_INIT1, IS_INIT2, IS_INIT3, IS_INIT4, IS_JMP, IS_JMP_CMD,
       IS_LIKE_JMP_CMD, IS_NEXT, IS_OUT_CMD, IS_RDY, IS_SHOW, IS_SIMPLE_CMD, IS_SKIP, IS_STOP, IS_STOP_CMD,
       IS_WHCHK, IS_WHGET, IS_WHILE, IS_WHILE_CMD, not_1_out, not_2_out, not_3_out, not_4_out, not_5_out,
       not_6_out, not_7_out, or_1_out, or_2_out, STOP_SKIP;
  wire [2:0] NEXT_CMD;
  wire [6:0] CUR_STATE;
  wire [7:0] counter_1_q, NEXT_STATE, NEXT_TO_CELL;
  wire [7:7] DISP_t;

  not not_1 (not_1_out, CLK);
  not not_2 (not_2_out, CLK);
  or or_1 (or_1_out, IS_JMP, IS_SKIP);
  Register STATE (.D(NEXT_STATE), .Q({IS_INITED, CUR_STATE}), .clk(not_1_out));  // open: en, clr
  Register CELL_DATA (.D(NEXT_TO_CELL), .Q(DATA_TO_CELL), .clk(not_2_out));  // open: en, clr
  and and_1 (and_1_out, IS_INIT0, IS_ON);
  assign NEXT_STATE = and_1_out ? 8'h1 : 8'bz;  // Controlled_Buffer controlled_buffer_1
  assign NEXT_STATE = IS_INIT3 ? 8'h4 : 8'bz;  // Controlled_Buffer controlled_buffer_2
  assign NEXT_CMD = IS_INIT3 ? 3'b011 : 3'bz;  // Controlled_Buffer controlled_buffer_3
  not not_3 (not_3_out, HAS_CHAR);
  assign NEXT_STATE = IS_SHOW ? 8'h82 : 8'bz;  // Controlled_Buffer controlled_buffer_4
  assign TTY_CLK = IS_SHOW ? CLK : 1'bz;  // Controlled_Buffer controlled_buffer_5
  assign {DISP_t[7], DISP} = IS_SHOW ? DATA_FROM_CELL : 8'bz;  // Controlled_Buffer controlled_buffer_6
  and and_2 (and_2_out, HAS_CHAR, IS_EXECW0);
  assign NEXT_STATE = and_2_out ? 8'h85 : 8'bz;  // Controlled_Buffer controlled_buffer_7
  and and_3 (and_3_out, HAS_CHAR, IS_EXECW0);
  assign NEXT_TO_CELL = and_3_out ? {1'b0, CHAR} : 8'bz;  // Controlled_Buffer controlled_buffer_8
  buf buffer_1 (WAIT_KBD, IS_EXECW0);
  not not_4 (not_4_out, CELL_ZERO);
  and and_4 (and_4_out, IS_WHILE_CMD, or_1_out);
  and and_5 (and_5_out, or_1_out, IS_JMP_CMD);
  Comparator #(.mode("unsigned")) comparator_1 (
    .a({IS_INITED, CUR_STATE}), .b({8{1'b0}}), .eq(IS_INIT0));  // open: gt, lt
  Comparator #(.mode("unsigned")) comparator_2 (.a({IS_INITED, CUR_STATE}), .b(8'h2), .eq(IS_INIT2));  // open: gt, lt
  Comparator #(.mode("unsigned")) comparator_3 (.a({IS_INITED, CUR_STATE}), .b(8'h4), .eq(IS_INIT4));  // open: gt, lt
  Comparator #(.mode("unsigned")) comparator_4 (.a({IS_INITED, CUR_STATE}), .b(8'h80), .eq(IS_RDY));  // open: gt, lt
  Comparator #(.mode("unsigned")) comparator_5 (.a({IS_INITED, CUR_STATE}), .b(8'h82), .eq(IS_NEXT));  // open: gt, lt
  Comparator #(.mode("unsigned")) comparator_6 (.a({IS_INITED, CUR_STATE}), .b(8'h84), .eq(IS_EXECW0));  // open: gt, lt
  Comparator #(.mode("unsigned")) comparator_7 (.a({IS_INITED, CUR_STATE}), .b(8'h86), .eq(IS_SHOW));  // open: gt, lt
  Comparator #(.mode("unsigned")) comparator_8 (.a({IS_INITED, CUR_STATE}), .b(8'h88), .eq(IS_JMP));  // open: gt, lt
  Comparator #(.mode("unsigned")) comparator_9 (.a({IS_INITED, CUR_STATE}), .b(8'h8a), .eq(IS_WHGET));  // open: gt, lt
  Comparator #(.mode("unsigned")) comparator_10 (.a({IS_INITED, CUR_STATE}), .b(8'h6), .eq(IS_STOP));  // open: gt, lt
  Pull_Resistor pull_resistor_1 (.node(CLK));
  Hex_Digit_Display hex_digit_display_1 (.value(DATA_TO_CELL[7:4]));  // open: dp
  and and_6 (and_6_out, IS_SIMPLE_CMD, IS_RDY);
  assign NEXT_STATE = and_6_out ? 8'h81 : 8'bz;  // Controlled_Buffer controlled_buffer_9
  and and_7 (and_7_out, IS_IN_CMD, not_3_out, IS_RDY);
  assign NEXT_STATE = and_7_out ? 8'h84 : 8'bz;  // Controlled_Buffer controlled_buffer_10
  and and_8 (and_8_out, IS_WHILE_CMD, IS_RDY);
  assign NEXT_STATE = and_8_out ? 8'h8a : 8'bz;  // Controlled_Buffer controlled_buffer_11
  and and_9 (and_9_out, IS_WHILE_CMD, IS_RDY);
  assign NEXT_CMD = and_9_out ? 3'b100 : 3'bz;  // Controlled_Buffer controlled_buffer_12
  and and_10 (and_10_out, IS_WHCHK, CELL_ZERO);
  assign NEXT_STATE = and_10_out ? 8'h89 : 8'bz;  // Controlled_Buffer controlled_buffer_13
  and and_11 (and_11_out, IS_WHCHK, not_4_out);
  assign NEXT_STATE = and_11_out ? 8'h82 : 8'bz;  // Controlled_Buffer controlled_buffer_14
  or or_2 (or_2_out, and_4_out, and_5_out);
  Hex_Digit_Display hex_digit_display_2 (.value(DATA_TO_CELL[3:0]));  // open: dp
  Counter counter_1 (.load(and_4_out), .count(or_2_out), .Q(counter_1_q), .clk(or_2_out));  // open: D, carry, clr
  assign NEXT_STATE = IS_EXEC ? 8'h82 : 8'bz;  // Controlled_Buffer controlled_buffer_15
  assign CELL_CLK = IS_EXEC ? CLK : 1'bz;  // Controlled_Buffer controlled_buffer_16
  Comparator #(.mode("unsigned")) comparator_11 (.a(counter_1_q), .b({8{1'b0}}), .eq(STOP_SKIP));  // open: gt, lt
  Comparator #(.mode("unsigned")) comparator_12 (.a({IS_INITED, CUR_STATE}), .b(8'h1), .eq(IS_INIT1));  // open: gt, lt
  Comparator #(.mode("unsigned")) comparator_13 (.a({IS_INITED, CUR_STATE}), .b(8'h3), .eq(IS_INIT3));  // open: gt, lt
  Comparator #(.mode("unsigned")) comparator_14 (.a({IS_INITED, CUR_STATE}), .b(8'h5), .eq(CLEAR_ACT));  // open: gt, lt
  Comparator #(.mode("unsigned")) comparator_15 (.a({IS_INITED, CUR_STATE}), .b(8'h81), .eq(IS_EXEC));  // open: gt, lt
  Comparator #(.mode("unsigned")) comparator_16 (.a({IS_INITED, CUR_STATE}), .b(8'h83), .eq(IS_EXECR));  // open: gt, lt
  Comparator #(.mode("unsigned")) comparator_17 (
    .a({IS_INITED, CUR_STATE}), .b(8'h85), .eq(IS_EXECW1));  // open: gt, lt
  Comparator #(.mode("unsigned")) comparator_18 (.a({IS_INITED, CUR_STATE}), .b(8'h87), .eq(IS_WHILE));  // open: gt, lt
  Comparator #(.mode("unsigned")) comparator_19 (.a({IS_INITED, CUR_STATE}), .b(8'h89), .eq(IS_SKIP));  // open: gt, lt
  Comparator #(.mode("unsigned")) comparator_20 (.a({IS_INITED, CUR_STATE}), .b(8'h8b), .eq(IS_WHCHK));  // open: gt, lt
  D_Flip_Flop d_ff_1 (.Q(FAKE_ACT), .preset(IS_INIT2), .reset(CLEAR_ACT));  // open: clk, D, Qn, en
  assign NEXT_STATE = IS_INIT1 ? 8'h2 : 8'bz;  // Controlled_Buffer controlled_buffer_17
  assign NEXT_CMD = IS_INIT1 ? 3'b001 : 3'bz;  // Controlled_Buffer controlled_buffer_18
  assign NEXT_STATE = IS_INIT4 ? 8'h5 : 8'bz;  // Controlled_Buffer controlled_buffer_19
  assign CELL_CLK = IS_INIT4 ? CLK : 1'bz;  // Controlled_Buffer controlled_buffer_20
  assign NEXT_STATE = IS_EXECW1 ? 8'h82 : 8'bz;  // Controlled_Buffer controlled_buffer_21
  assign CELL_CLK = IS_EXECW1 ? CLK : 1'bz;  // Controlled_Buffer controlled_buffer_22
  assign KBD_CLK = IS_EXECW1 ? CLK : 1'bz;  // Controlled_Buffer controlled_buffer_23
  Register #(.width(3)) CELL_CMD (.D(NEXT_CMD), .Q(CMD), .clk(not_5_out));  // open: en, clr
  not not_5 (not_5_out, CLK);
  and and_12 (and_12_out, IS_OUT_CMD, IS_RDY);
  assign NEXT_STATE = and_12_out ? 8'h83 : 8'bz;  // Controlled_Buffer controlled_buffer_24
  and and_13 (and_13_out, IS_IN_CMD, HAS_CHAR, IS_RDY);
  assign NEXT_STATE = and_13_out ? 8'h85 : 8'bz;  // Controlled_Buffer controlled_buffer_25
  and and_14 (and_14_out, IS_JMP_CMD, IS_RDY);
  assign NEXT_STATE = and_14_out ? 8'h88 : 8'bz;  // Controlled_Buffer controlled_buffer_26
  and and_15 (and_15_out, IS_SKIP, STOP_SKIP);
  assign TAPE_NEXT = IS_SKIP ? CLK : 1'bz;  // Controlled_Buffer controlled_buffer_27
  assign NEXT_STATE = and_15_out ? 8'h82 : 8'bz;  // Controlled_Buffer controlled_buffer_28
  Pull_Resistor pull_resistor_2 (.node(HAS_CHAR));
  Hex_Digit_Display hex_digit_display_3 (.value({1'b0, CMD}));  // open: dp
  assign NEXT_STATE = IS_NEXT ? 8'h80 : 8'bz;  // Controlled_Buffer controlled_buffer_29
  assign TAPE_NEXT = IS_NEXT ? CLK : 1'bz;  // Controlled_Buffer controlled_buffer_30
  Pull_Resistor pull_resistor_3 (.node(CELL_ZERO));
  Comparator #(.mode("unsigned")) comparator_21 (.a(DATA_FROM_CELL), .b({8{1'b0}}), .eq(CELL_ZERO));  // open: gt, lt
  Comparator #(.width(3), .mode("unsigned")) comparator_22 (
    .a(CUR_BF[2:0]), .b(3'b000), .eq(comparator_22_eq));  // open: gt, lt
  not not_6 (not_6_out, CUR_BF[3]);
  Comparator #(.width(3), .mode("unsigned")) comparator_23 (
    .a(CUR_BF[2:0]), .b(3'b001), .eq(IS_WHILE_CMD));  // open: gt, lt
  buf buffer_2 (IS_SIMPLE_CMD, CUR_BF[1]);
  Comparator #(.width(3), .mode("unsigned")) comparator_24 (
    .a(CUR_BF[2:0]), .b(3'b100), .eq(IS_OUT_CMD));  // open: gt, lt
  Comparator #(.width(3), .mode("unsigned")) comparator_25 (
    .a(CUR_BF[2:0]), .b(3'b101), .eq(IS_IN_CMD));  // open: gt, lt
  buf buffer_3 (IS_STOP_CMD, CUR_BF[3]);
  or or_3 (IS_LIKE_JMP_CMD, IS_JMP_CMD, IS_WHILE_CMD);
  D_Flip_Flop d_ff_2 (.Q(IS_ON), .preset(TURN_ON), .reset(IS_STOP));  // open: clk, D, Qn, en
  assign NEXT_STATE = IS_INIT2 ? 8'h3 : 8'bz;  // Controlled_Buffer controlled_buffer_31
  assign CELL_CLK = IS_INIT2 ? CLK : 1'bz;  // Controlled_Buffer controlled_buffer_32
  assign NEXT_STATE = CLEAR_ACT ? 8'h80 : 8'bz;  // Controlled_Buffer controlled_buffer_33
  assign NEXT_CMD = CLEAR_ACT ? 3'b000 : 3'bz;  // Controlled_Buffer controlled_buffer_34
  assign NEXT_STATE = IS_WHGET ? 8'h8b : 8'bz;  // Controlled_Buffer controlled_buffer_35
  assign CELL_CLK = IS_WHGET ? CLK : 1'bz;  // Controlled_Buffer controlled_buffer_36
  and and_16 (IS_JMP_CMD, comparator_22_eq, not_6_out);
  not not_7 (not_7_out, IS_LIKE_JMP_CMD);
  and and_17 (and_17_out, IS_IN_CMD, HAS_CHAR, IS_RDY);
  and and_18 (and_18_out, CUR_BF[3], IS_RDY);
  and and_19 (and_19_out, not_7_out, IS_RDY);
  assign NEXT_CMD = and_19_out ? CUR_BF[2:0] : 3'bz;  // Controlled_Buffer controlled_buffer_37
  assign NEXT_TO_CELL = and_17_out ? {1'b0, CHAR} : 8'bz;  // Controlled_Buffer controlled_buffer_38
  assign NEXT_STATE = and_18_out ? 8'h6 : 8'bz;  // Controlled_Buffer controlled_buffer_39
  assign TAPE_PREV = IS_JMP ? CLK : 1'bz;  // Controlled_Buffer controlled_buffer_40
  and and_20 (and_20_out, IS_JMP, STOP_SKIP);
  assign NEXT_STATE = and_20_out ? 8'h80 : 8'bz;  // Controlled_Buffer controlled_buffer_41
  assign NEXT_STATE = IS_EXECR ? 8'h86 : 8'bz;  // Controlled_Buffer controlled_buffer_42
  assign CELL_CLK = IS_EXECR ? CLK : 1'bz;  // Controlled_Buffer controlled_buffer_43

  // Other names for the same wires on the sheet: CELL_CMD[2:0] = CMD; CHAR_t[6:0] = CHAR;
  //   CUR_BF_CMD[2:0] = CUR_BF[2:0]; STOP_FLAG = CUR_BF[3]; RESERVED[6:0] = CUR_STATE; CUR_STATE[7] = IS_INITED;
  //   STATE_INITED = IS_INITED; DISP_t[6:0] = DISP; FROM_CELL[7:0] = DATA_FROM_CELL; IS_INIT5 = CLEAR_ACT;
  //   SET_ACT = IS_INIT2; TO_CELL[7:0] = DATA_TO_CELL
endmodule
